// Logisim project EJ 2.1.circ as structural Verilog
module ej_2_1 (
  input  [3:0] A,
  input  [3:0] B,
  output [4:0] out_3
);

  wire and_1_out, or_2_out;
  wire [2:2] or_1_out;
  wire [3:0] adder_1_out;
  wire [4:4] adder_1_cout;

  Adder #(.width(4)) adder_1 (.a(A), .b(B), .out(adder_1_out), .cout(adder_1_cout[4]));  // open: cin
  or or_1 (or_1_out[2], and_1_out, adder_1_cout[4]);
  or or_2 (or_2_out, adder_1_out[1], adder_1_out[2]);
  and and_1 (and_1_out, or_2_out, adder_1_out[3]);
  Adder #(.width(5)) adder_2 (
    .a({2'b00, {2{or_1_out[2]}}, 1'b0}), .b({adder_1_cout[4], adder_1_out}), .out(out_3));  // open: cin, cout
endmodule

module ej_2_2 (
  input  [3:0] A,
  input  [3:0] B,
  input  [3:0] C,
  output [4:0] out_4
);

  wire comparator_1_eq, comparator_1_lt;
  wire [3:0] adder_1_out, and_1_out, and_2_out;
  wire [3:3] comparator_1_gt, or_1_out;

  Comparator #(.width(4), .mode("unsigned")) comparator_1 (
    .a(B), .b(C), .gt(comparator_1_gt[3]), .eq(comparator_1_eq), .lt(comparator_1_lt));
  or or_1 (or_1_out[3], comparator_1_eq, comparator_1_lt);
  assign and_1_out = B & {4{comparator_1_gt[3]}};  // AND_Gate and_1, 4 bits wide
  assign and_2_out = {4{or_1_out[3]}} & C;  // AND_Gate and_2, 4 bits wide
  ej_2_1 ej_2_1_1 (.A(A), .B(adder_1_out), .out_3(out_4));
  Adder #(.width(4)) adder_1 (.a(and_1_out), .b(and_2_out), .out(adder_1_out));  // open: cin, cout
endmodule
