// Logisim project EJ 3.3.circ as structural Verilog: 2 circuits, main circuit A
module A (
  input  [1:0] in_1,
  input  clk,
  input  D,
  input  C,
  input  B,
  input  A,
  input  CLEAR,
  output S_C,
  output S_B,
  output S_A,
  output S_D
);

  wire multiplexer_1_out, multiplexer_2_out, multiplexer_3_out, multiplexer_4_out;

  Multiplexer #(.select(2)) multiplexer_1 (
    .in0(S_D), .in1(S_A), .in2(S_C), .in3(D), .out(multiplexer_1_out), .sel(in_1));  // open: en
  D_Flip_Flop d_ff_1 (.clk(clk), .D(multiplexer_1_out), .Q(S_D), .reset(CLEAR));  // open: Qn, preset, en
  Multiplexer #(.select(2)) multiplexer_2 (
    .in0(S_C), .in1(S_D), .in2(S_B), .in3(C), .out(multiplexer_2_out), .sel(in_1));  // open: en
  D_Flip_Flop d_ff_2 (.clk(clk), .D(multiplexer_2_out), .Q(S_C), .reset(CLEAR));  // open: Qn, preset, en
  Multiplexer #(.select(2)) multiplexer_3 (
    .in0(S_B), .in1(S_C), .in2(S_A), .in3(B), .out(multiplexer_3_out), .sel(in_1));  // open: en
  D_Flip_Flop d_ff_3 (.clk(clk), .D(multiplexer_3_out), .Q(S_B), .reset(CLEAR));  // open: Qn, preset, en
  Multiplexer #(.select(2)) multiplexer_4 (
    .in0(S_A), .in1(S_B), .in2(S_D), .in3(A), .out(multiplexer_4_out), .sel(in_1));  // open: en
  D_Flip_Flop d_ff_4 (.clk(clk), .D(multiplexer_4_out), .Q(S_A), .reset(CLEAR));  // open: Qn, preset, en

  // Other names for the same wires on the sheet: DSL = S_D; DSR = S_A
endmodule

module B (
  input  A,
  input  B,
  input  C,
  input  D,
  output S_A,
  output S_B,
  output S_C,
  output S_D
);

  wire and_1_out, clock_1_out, not_1_out;
  wire [1:0] not_2_out;
  wire [2:0] counter_1_q;

  Clock clock_1 (.out(clock_1_out));
  Counter #(.width(3), .max('h4)) counter_1 (
    .load(1'b0), .count(1'b1), .Q(counter_1_q), .clk(clock_1_out));  // open: D, carry, clr
  not not_1 (not_1_out, clock_1_out);
  A a_1 (
    .in_1(not_2_out), .clk(not_1_out), .CLEAR(and_1_out), .D(D), .C(C), .B(B), .A(A), .S_D(S_D), .S_C(S_C),
    .S_B(S_B), .S_A(S_A));
  or or_1 (not_2_out[1], counter_1_q[0], counter_1_q[1], counter_1_q[2]);
  not not_2 (not_2_out[0], counter_1_q[1]);
  and and_1 (and_1_out, counter_1_q[0], counter_1_q[1]);
endmodule
