// Logisim project EJ 3.circ as structural Verilog
module Ej_2 (
  input  A,
  input  B,
  input  C,
  input  D,
  output F1,
  output F2,
  output F2_2
);

  wire nand_1_out, nand_2_out, nor_1_out, nor_2_out, or_1_out;

  or or_1 (or_1_out, B, C);
  nor nor_1 (nor_1_out, A, A);
  nor nor_2 (nor_2_out, B, C);
  nand nand_1 (nand_1_out, A, B);
  nand nand_2 (nand_2_out, A, C);
  and and_1 (F1, A, or_1_out);
  nor nor_3 (F2, nor_1_out, nor_2_out);
  nand nand_3 (F2_2, nand_1_out, nand_2_out);
endmodule

module \semáforos  (
  input  A,
  input  B,
  input  C,
  input  D,
  output SA,
  output SB,
  output SC,
  output SD
);

  wire and_1_out, and_2_out, and_3_out, and_4_out, and_5_out, and_6_out, and_7_out, and_8_out, and_9_out,
       and_10_out, and_11_out, and_12_out, not_1_out, not_2_out, not_3_out, not_4_out;

  not not_1 (not_1_out, A);
  not not_2 (not_2_out, B);
  not not_3 (not_3_out, D);
  not not_4 (not_4_out, C);
  and and_1 (and_1_out, not_1_out, not_2_out, C);
  and and_2 (and_2_out, not_1_out, B, not_4_out);
  and and_3 (and_3_out, A, not_2_out, not_4_out);
  and and_4 (and_4_out, not_1_out, B, not_4_out, not_3_out);
  and and_5 (and_5_out, not_2_out, D);
  and and_6 (and_6_out, A, C);
  and and_7 (and_7_out, A, B);
  and and_8 (and_8_out, not_2_out, not_4_out, D);
  and and_9 (and_9_out, not_2_out, C, not_3_out);
  and and_10 (and_10_out, C, D);
  and and_11 (and_11_out, B, D);
  and and_12 (and_12_out, B, C);
  or or_1 (SA, and_1_out, and_2_out, and_3_out);
  or or_2 (SB, and_4_out, and_5_out, and_6_out);
  or or_3 (SC, and_7_out, and_8_out, and_9_out);
  or or_4 (SD, and_10_out, and_11_out, and_12_out);
endmodule

module ej_3 (
  input  A1,
  input  B1,
  input  C1,
  input  D1,
  input  A2,
  input  B2,
  input  C2,
  input  D2,
  output out_9
);

  wire ej_2_1_f1, ej_2_2_f1;

  Ej_2 ej_2_1 (.A(A1), .B(B1), .C(C1), .D(D1), .F1(ej_2_1_f1));  // open: F2, F2_2
  Ej_2 ej_2_2 (.A(A2), .B(B2), .C(C2), .D(D2), .F1(ej_2_2_f1));  // open: F2, F2_2
  or or_1 (out_9, ej_2_1_f1, ej_2_2_f1);
endmodule
