// Logisim project EJ 4.circ as structural Verilog
module ej4_parte_1 (
  input  A,
  input  S1,
  input  S2,
  output M1,
  output M2,
  output ERROR
);

  wire nor_1_out, nor_2_out, nor_3_out;

  nor nor_1 (nor_1_out, S1, S1);
  nor nor_2 (nor_2_out, A, A);
  nor nor_3 (nor_3_out, S2, S2);
  nor nor_4 (M1, nor_1_out, nor_2_out);
  nor nor_5 (M2, nor_2_out, nor_3_out);
  nor nor_6 (ERROR, nor_2_out, nor_3_out, S1);
endmodule
