// Logisim project EJ 5.circ as structural Verilog
module ej_5 (
  input  A,
  input  D,
  input  t1,
  input  t0,
  output E,
  output C
);

  wire and_1_out, nand_1_out, nand_2_out, not_1_out;

  not not_1 (not_1_out, D);
  nand nand_1 (nand_1_out, A, t0);
  nand nand_2 (nand_2_out, t0, not_1_out);
  and and_1 (and_1_out, not_1_out, A);
  and and_2 (E, nand_1_out, t1, nand_2_out);
  nor nor_1 (C, and_1_out, t1, t0);
endmodule
