// Logisim project ej 2.3.circ as structural Verilog: 1 circuit, main circuit main
module main (
  input  C1_C2,
  input  SUMA_RESTA,
  input  [3:0] B,
  input  [3:0] A,
  output [3:0] out_5,
  output out_6
);

  wire adder_1_cout, and_1_out, and_2_out, and_3_out, and_4_out, not_1_out, not_2_out, not_3_out, not_4_out;
  wire [3:0] adder_1_out, xor_1_out;

  assign xor_1_out = {4{SUMA_RESTA}} ^ B;  // XOR_Gate xor_1, 4 bits wide
  and and_1 (and_1_out, SUMA_RESTA, C1_C2);
  Adder #(.width(4)) adder_1 (.a(xor_1_out), .b(A), .out(adder_1_out), .cin(and_1_out), .cout(adder_1_cout));
  not not_1 (not_1_out, C1_C2);
  and and_2 (and_2_out, not_1_out, adder_1_cout);
  Adder #(.width(4)) adder_2 (.a(adder_1_out), .b(4'b0000), .out(out_5), .cin(and_2_out));  // open: cout
  not not_2 (not_2_out, xor_1_out[3]);
  not not_3 (not_3_out, A[3]);
  and and_3 (and_3_out, not_2_out, not_3_out, out_5[3]);
  not not_4 (not_4_out, out_5[3]);
  or or_1 (out_6, and_3_out, and_4_out);
  and and_4 (and_4_out, xor_1_out[3], A[3], not_4_out);
endmodule
