// Logisim project ej 2.4.circ as structural Verilog: 1 circuit, main circuit main
module main (
  input  [3:0] A,
  input  [3:0] B,
  input  [3:0] C,
  output [3:0] S,
  output [1:0] N
);

  wire comparator_1_lt;
  wire [3:0] and_1_out, and_2_out, and_3_out;
  wire [3:3] comparator_1_eq, comparator_2_eq, comparator_3_eq;

  Comparator #(.width(4), .mode("unsigned")) comparator_1 (
    .a(A), .b(B), .eq(comparator_1_eq[3]), .lt(comparator_1_lt));  // open: gt
  Comparator #(.width(4), .mode("unsigned")) comparator_2 (.a(B), .b(C), .eq(comparator_2_eq[3]));  // open: gt, lt
  Comparator #(.width(4), .mode("unsigned")) comparator_3 (.a(A), .b(C), .eq(comparator_3_eq[3]));  // open: gt, lt
  assign and_1_out = A & {4{comparator_1_eq[3]}};  // AND_Gate and_1, 4 bits wide
  assign and_2_out = B & {4{comparator_2_eq[3]}};  // AND_Gate and_2, 4 bits wide
  assign and_3_out = C & {4{comparator_3_eq[3]}};  // AND_Gate and_3, 4 bits wide
  and and_4 (N[0], comparator_1_eq[3], comparator_2_eq[3]);
  or or_1 (N[1], comparator_1_eq[3], comparator_2_eq[3], comparator_3_eq[3]);
  assign S = and_1_out | and_2_out | and_3_out;  // OR_Gate or_2, 4 bits wide
endmodule
