// Logisim project ej 2.5.2circ.circ as structural Verilog: 1 circuit, main circuit main
module main (
  input  [3:0] A,
  input  [3:0] B,
  input  [1:0] SM_11_C1_00_C2_01,
  output A_B,
  output A_B_2,
  output A_B_3
);

  wire and_1_out, and_2_out, and_3_out, and_4_out, and_5_out, and_6_out, and_7_out, and_8_out, and_9_out,
       and_10_out, and_11_out, and_12_out, and_13_out, comparator_1_eq, comparator_1_gt, comparator_1_lt,
       comparator_2_eq, comparator_2_gt, comparator_2_lt, comparator_3_eq, comparator_4_eq, nor_1_out,
       not_1_out, not_3_out, not_4_out, not_5_out, or_1_out, or_2_out, or_3_out, or_4_out, xor_1_out,
       xor_2_out;
  wire [3:0] not_2_out;

  and and_1 (and_1_out, SM_11_C1_00_C2_01[1], SM_11_C1_00_C2_01[0]);
  Comparator #(.width(1), .mode("unsigned")) comparator_1 (
    .a(A[3]), .b(B[3]), .gt(comparator_1_gt), .eq(comparator_1_eq), .lt(comparator_1_lt));
  Comparator #(.width(3), .mode("unsigned")) comparator_2 (
    .a(A[2:0]), .b(B[2:0]), .gt(comparator_2_gt), .eq(comparator_2_eq), .lt(comparator_2_lt));
  and and_2 (and_2_out, SM_11_C1_00_C2_01[1], B[3]);
  nor nor_1 (nor_1_out, SM_11_C1_00_C2_01[0], SM_11_C1_00_C2_01[1]);
  not not_1 (not_1_out, comparator_1_eq);
  assign not_2_out = ~B;  // NOT_Gate not_2, 4 bits wide
  Comparator #(.width(3), .mode("unsigned")) comparator_3 (
    .a(B[2:0]), .b(A[2:0]), .eq(comparator_3_eq));  // open: gt, lt
  xor xor_1 (xor_1_out, comparator_2_gt, and_2_out);
  not not_3 (not_3_out, comparator_2_eq);
  xor xor_2 (xor_2_out, comparator_2_lt, and_2_out);
  Comparator #(.width(4), .mode("unsigned")) comparator_4 (.a(not_2_out), .b(A), .eq(comparator_4_eq));  // open: gt, lt
  and and_3 (and_3_out, and_1_out, comparator_3_eq);
  and and_4 (and_4_out, xor_1_out, not_3_out);
  and and_5 (and_5_out, not_3_out, xor_2_out);
  and and_6 (and_6_out, nor_1_out, comparator_4_eq);
  and and_7 (and_7_out, comparator_1_eq, and_4_out);
  and and_8 (and_8_out, comparator_1_eq, comparator_2_eq);
  and and_9 (and_9_out, comparator_1_eq, and_5_out);
  or or_1 (or_1_out, and_9_out, comparator_1_gt);
  or or_2 (or_2_out, comparator_1_lt, and_7_out);
  and and_10 (and_10_out, not_4_out, or_1_out);
  and and_11 (and_11_out, not_4_out, or_2_out);
  or or_3 (or_3_out, and_8_out, and_6_out);
  not not_4 (not_4_out, and_6_out);
  and and_12 (and_12_out, or_1_out, not_5_out);
  and and_13 (and_13_out, or_2_out, not_5_out);
  not not_5 (not_5_out, and_3_out);
  and and_14 (A_B, and_10_out, and_12_out);
  and and_15 (A_B_2, and_11_out, and_13_out);
  or or_4 (or_4_out, and_3_out, and_8_out);
  or or_5 (A_B_3, or_3_out, or_4_out);
endmodule
