// Logisim project ej 2.5.circ as structural Verilog: 1 circuit, main circuit main
module main (
  input  [3:0] A,
  input  [3:0] B,
  input  [1:0] SM_11_C1_01_C2_00,
  output A_B,
  output A_B_2,
  output A_B_3
);

  wire and_1_out, and_2_out, and_3_out, and_4_out, and_6_out, comparator_1_eq, comparator_1_gt,
       comparator_1_lt, comparator_2_eq, comparator_2_gt, comparator_2_lt, not_1_out, xor_1_out, xor_2_out;

  Comparator #(.width(1), .mode("unsigned")) comparator_1 (
    .a(A[3]), .b(B[3]), .gt(comparator_1_gt), .eq(comparator_1_eq), .lt(comparator_1_lt));
  Comparator #(.width(3), .mode("unsigned")) comparator_2 (
    .a(A[2:0]), .b(B[2:0]), .gt(comparator_2_gt), .eq(comparator_2_eq), .lt(comparator_2_lt));
  and and_1 (and_1_out, SM_11_C1_01_C2_00[1], B[3]);
  xor xor_1 (xor_1_out, comparator_2_gt, and_1_out);
  not not_1 (not_1_out, comparator_2_eq);
  xor xor_2 (xor_2_out, comparator_2_lt, and_1_out);
  and and_2 (and_2_out, xor_1_out, not_1_out);
  and and_3 (and_3_out, not_1_out, xor_2_out);
  and and_4 (and_4_out, comparator_1_eq, and_2_out);
  and and_5 (A_B_3, comparator_1_eq, comparator_2_eq);
  and and_6 (and_6_out, comparator_1_eq, and_3_out);
  or or_1 (A_B, and_6_out, comparator_1_gt);
  or or_2 (A_B_2, comparator_1_lt, and_4_out);
endmodule
