// Logisim project ej 2.6.circ as structural Verilog
module SUMADOR (
  input  A,
  input  B,
  input  C,
  output S,
  output Cout
);

  wire and_1_out, and_2_out, xor_1_out;

  xor xor_1 (xor_1_out, A, B);
  and and_1 (and_1_out, xor_1_out, C);
  and and_2 (and_2_out, A, B);
  xor xor_2 (S, xor_1_out, C);
  xor xor_3 (Cout, and_1_out, and_2_out);
endmodule

module SinPeso (
  input  C,
  input  C_2,
  input  C_3,
  input  S,
  input  P,
  output out_6,
  output out_7
);

  wire sumador_1_cout, sumador_1_s, sumador_2_cout, sumador_2_s, sumador_3_cout;
  wire [2:0] sumador_3_s;

  SUMADOR sumador_1 (.A(C), .B(C_2), .C(C_3), .S(sumador_1_s), .Cout(sumador_1_cout));
  SUMADOR sumador_2 (.A(S), .B(P), .C(1'b0), .S(sumador_2_s), .Cout(sumador_2_cout));
  SUMADOR sumador_3 (.A(sumador_1_s), .B(sumador_2_s), .C(1'b0), .S(sumador_3_s[0]), .Cout(sumador_3_cout));
  SUMADOR sumador_4 (
    .A(sumador_1_cout), .B(sumador_2_cout), .C(sumador_3_cout), .S(sumador_3_s[1]), .Cout(sumador_3_s[2]));
  Comparator #(.width(3)) comparator_1 (.a(sumador_3_s), .b(3'b010), .gt(out_6), .eq(out_7));  // open: lt
endmodule

module ConPeso (
  input  C,
  input  C_2,
  input  C_3,
  input  S,
  input  P,
  output out_6,
  output out_7
);

  wire sumador_1_cout, sumador_1_s, sumador_2_cout, sumador_3_cout;
  wire [3:0] sumador_2_s;

  SUMADOR sumador_1 (.A(C), .B(C_2), .C(C_3), .S(sumador_1_s), .Cout(sumador_1_cout));
  SUMADOR sumador_2 (.A(sumador_1_s), .B(S), .C(1'b0), .S(sumador_2_s[0]), .Cout(sumador_2_cout));
  SUMADOR sumador_3 (.A(sumador_2_cout), .B(sumador_1_cout), .C(S), .S(sumador_2_s[1]), .Cout(sumador_3_cout));
  SUMADOR sumador_4 (.A(sumador_3_cout), .B(P), .C(1'b0), .S(sumador_2_s[2]), .Cout(sumador_2_s[3]));
  Comparator #(.width(4)) comparator_1 (.a(sumador_2_s), .b(4'b0101), .gt(out_6), .eq(out_7));  // open: lt
endmodule
