// Logisim project ej 3.1.3.circ as structural Verilog: 1 circuit, main circuit main
module main (
  input  [1:0] in_1,
  output Lata,
  output Cambio
);

  wire and_1_out, and_2_out, and_3_out, and_4_out, and_5_out, and_6_out, and_7_out, and_8_out, and_9_out,
       and_10_out, and_11_out, clock_1_out, D0_q, D0_qn, D1_q, D1_qn, not_1_out, not_2_out, or_1_out,
       or_2_out;

  Clock clock_1 (.out(clock_1_out));
  not not_1 (not_1_out, in_1[0]);
  not not_2 (not_2_out, in_1[1]);
  and and_1 (and_1_out, in_1[0], not_2_out, D1_qn, D0_qn);
  and and_2 (and_2_out, D0_q, not_2_out, not_1_out);
  or or_1 (or_1_out, and_1_out, and_2_out);
  and and_3 (and_3_out, D0_qn, D1_qn, in_1[1], not_1_out);
  and and_4 (and_4_out, D0_q, not_2_out, in_1[0]);
  or or_2 (or_2_out, and_3_out, and_4_out, and_5_out);
  and and_5 (and_5_out, not_2_out, not_1_out, D1_q);
  D_Flip_Flop D0 (.clk(clock_1_out), .D(or_1_out), .Q(D0_q), .Qn(D0_qn));  // open: preset, en, reset
  D_Flip_Flop D1 (.clk(clock_1_out), .D(or_2_out), .Q(D1_q), .Qn(D1_qn));  // open: preset, en, reset
  and and_6 (and_6_out, in_1[0], in_1[1]);
  and and_7 (and_7_out, in_1[0], D1_q);
  and and_8 (and_8_out, D0_q, in_1[1]);
  and and_9 (and_9_out, D1_q, in_1[1]);
  and and_10 (and_10_out, in_1[0], in_1[1]);
  and and_11 (and_11_out, D1_q, in_1[1]);
  or or_3 (Lata, and_6_out, and_7_out, and_8_out, and_9_out);
  or or_4 (Cambio, and_10_out, and_11_out);
endmodule
