// Logisim project ej 3.1.circ as structural Verilog: 1 circuit, main circuit main
module main (
  input  [1:0] in_1,
  output Cambio,
  output Lata
);

  wire _0_q, _0_qn, _1_q, _1_qn, and_1_out, and_2_out, and_3_out, and_4_out, and_5_out, clock_1_out,
       not_1_out, not_2_out, or_1_out;

  Clock clock_1 (.out(clock_1_out));
  not not_1 (not_1_out, in_1[0]);
  not not_2 (not_2_out, in_1[1]);
  and and_1 (and_1_out, not_1_out, not_2_out, _0_q);
  and and_2 (and_2_out, in_1[0], _0_qn, _1_qn);
  or or_1 (or_1_out, and_1_out, and_2_out);
  and and_3 (and_3_out, not_1_out, not_2_out, _1_qn, _0_qn);
  D_Flip_Flop _1 (.clk(clock_1_out), .D(or_1_out), .Q(_1_q), .Qn(_1_qn));  // open: preset, en, reset
  D_Flip_Flop _0 (.clk(clock_1_out), .D(and_3_out), .Q(_0_q), .Qn(_0_qn));  // open: preset, en, reset
  and and_4 (and_4_out, _0_q, in_1[0]);
  or or_2 (Cambio, in_1[1], and_5_out);
  and and_5 (and_5_out, in_1[0], _1_q);
  or or_3 (Lata, _1_q, in_1[1], and_4_out);
endmodule
