// Logisim project ej 3.4,3.5.circ as structural Verilog: 2 circuits, main circuit ej 3.4
module ej_3_4 (
  output S2,
  output S1,
  output S0
);

  wire _0_q, _1_q, _1_qn, _2_q, _2_qn, and_1_out, and_2_out, and_3_out, and_4_out, and_5_out, and_6_out,
       clock_1_out;

  Clock clock_1 (.out(clock_1_out));
  and and_1 (and_1_out, _1_q, _0_q);
  and and_2 (and_2_out, _2_qn, _0_q);
  J_K_Flip_Flop _2 (.J(and_1_out), .clk(clock_1_out), .K(_0_q), .Q(_2_q), .Qn(_2_qn));  // open: preset, en, reset
  J_K_Flip_Flop _1 (.J(and_2_out), .clk(clock_1_out), .K(_0_q), .Q(_1_q), .Qn(_1_qn));  // open: preset, en, reset
  J_K_Flip_Flop _0 (.J(1'b1), .clk(clock_1_out), .K(1'b1), .Q(_0_q), .Qn(S2));  // open: preset, en, reset
  and and_3 (and_3_out, _0_q, _1_qn, _2_qn);
  and and_4 (and_4_out, S2, _1_q);
  or or_1 (S1, and_3_out, and_4_out);
  and and_5 (and_5_out, _2_qn, _0_q);
  or or_2 (S0, and_5_out, and_6_out, _1_q);
  and and_6 (and_6_out, _2_q, S2);
endmodule

module ej_3_5 (
  output S2,
  output S1,
  output S0
);

  wire _0_q, _1_q, _1_qn, _2_q, _2_qn, and_1_out, and_2_out, and_3_out, and_4_out, and_5_out, and_6_out,
       and_7_out, and_8_out, and_9_out, and_10_out, and_11_out, and_12_out, and_13_out, and_14_out,
       clock_1_out, not_1_out, not_2_out, not_3_out, not_4_out, not_5_out, not_6_out, or_1_out, or_2_out,
       or_3_out;
  wire [2:0] counter_1_q;

  or or_1 (or_1_out, and_2_out, and_3_out, and_4_out);
  or or_2 (or_2_out, and_6_out, and_7_out);
  and and_1 (and_1_out, not_5_out, S2, S0);
  and and_2 (and_2_out, not_1_out, not_3_out, counter_1_q[0], not_4_out, not_5_out, not_6_out);
  and and_3 (and_3_out, not_1_out, counter_1_q[1], not_2_out, not_4_out, S1, S0);
  and and_4 (and_4_out, counter_1_q[2], not_3_out, not_2_out, not_4_out, not_5_out, S0);
  and and_5 (and_5_out, not_1_out, counter_1_q[1], not_2_out, not_4_out, S1, S0);
  and and_6 (and_6_out, not_1_out, counter_1_q[1], counter_1_q[0], S2, S1, S0);
  and and_7 (and_7_out, counter_1_q[2], not_3_out, not_2_out, not_4_out, not_5_out, S0);
  Counter #(.width(3), .max('h4)) counter_1 (
    .load(1'b0), .count(and_1_out), .Q(counter_1_q), .clk(clock_1_out));  // open: D, carry, clr
  not not_1 (not_1_out, counter_1_q[2]);
  Clock clock_1 (.out(clock_1_out));
  and and_8 (and_8_out, _1_q, _0_q);
  and and_9 (and_9_out, _2_qn, _0_q);
  not not_2 (not_2_out, counter_1_q[0]);
  not not_3 (not_3_out, counter_1_q[1]);
  or or_3 (or_3_out, or_1_out, and_10_out);
  and and_10 (and_10_out, S2, not_5_out, not_6_out);
  J_K_Flip_Flop _2 (
    .J(and_8_out), .clk(clock_1_out), .K(_0_q), .Q(_2_q), .Qn(_2_qn), .preset(or_2_out));  // open: en, reset
  J_K_Flip_Flop _1 (
    .J(and_9_out), .clk(clock_1_out), .K(_0_q), .Q(_1_q), .Qn(_1_qn), .preset(and_5_out));  // open: en, reset
  J_K_Flip_Flop _0 (.J(1'b1), .clk(clock_1_out), .K(1'b1), .Q(_0_q), .Qn(S2), .preset(or_3_out));  // open: en, reset
  not not_4 (not_4_out, S2);
  and and_11 (and_11_out, S2, _1_q);
  and and_12 (and_12_out, _0_q, _1_qn, _2_qn);
  or or_4 (S1, and_12_out, and_11_out);
  not not_5 (not_5_out, S1);
  not not_6 (not_6_out, S0);
  and and_13 (and_13_out, _2_qn, _0_q);
  or or_5 (S0, and_13_out, and_14_out, _1_q);
  and and_14 (and_14_out, _2_q, S2);
endmodule
