// Logisim project ej3.2.circ as structural Verilog: 1 circuit, main circuit main
module main (
  input  [1:0] in_1,
  output out_2
);

  wire _0_q, _1_qn, and_1_out, and_2_out, and_3_out, and_4_out, and_5_out, clock_1_out, not_1_out, or_1_out,
       or_2_out;

  Clock clock_1 (.out(clock_1_out));
  not not_1 (not_1_out, in_1[1]);
  and and_1 (and_1_out, in_1[0], out_2);
  and and_2 (and_2_out, in_1[1], _1_qn);
  or or_1 (or_1_out, and_1_out, and_2_out);
  and and_3 (and_3_out, out_2, in_1[0]);
  and and_4 (and_4_out, not_1_out, _0_q);
  and and_5 (and_5_out, out_2, _0_q);
  or or_2 (or_2_out, and_3_out, and_4_out, and_5_out);
  D_Flip_Flop _0 (.clk(clock_1_out), .D(or_1_out), .Q(_0_q));  // open: Qn, preset, en, reset
  D_Flip_Flop _1 (.clk(clock_1_out), .D(or_2_out), .Q(out_2), .Qn(_1_qn));  // open: preset, en, reset
endmodule
